# Fritzing sketch internal-joystick-groundout (saved by Fritzing 1.0.2b)
circuit board: 1.66573cm x 4.89834cm
breadboards: 1

parts:
  47k = Resistor [tolerance=±5% resistance=47k power=0.25W package=THT]
  U1 = ESP32S-HiLetgo [part_number=ESP32S-HiLetgo]
  47k_2 = Resistor [tolerance=±5% resistance=47k power=0.25W package=THT]
  47k_3 = Resistor [tolerance=±5% resistance=47k power=0.25W package=THT]
  47k_4 = Resistor [tolerance=±5% resistance=47k power=0.25W package=THT]

nets:
  N1: 47k.Pin_0, U1.GND, U1.GPIO9, 47k_2.Pin_0, 47k_3.Pin_0, 47k_4.Pin_0
  N2: 47k.Pin_1, U1.GPIO36
  N3: U1.GPIO39, 47k_2.Pin_1
  N4: U1.GPIO26, 47k_4.Pin_1
  N5: U1.GPIO27, 47k_3.Pin_1

notes:
  V1 - Retro6502.com
  Joystick Interface
  Ground Resistance
  GROUND
  26 - X
  27 - Y
  36 - B1
  39 - B0
  3.3v
  14 - LED
  retro6502.com

custom parts:
  ESP32S-HiLetgo: HiLetgo ESP-WROOM-32 ESP32 ESP-32S Development Board 2.4GHz Dual-Mode WiFi + Bluetooth Dual Cores Microcontroller The ESP32 integrated with Antenna switches, RF Balun, power amplifiers, low-noise amplifiers, filters, and management modules, and the entire solution occupies the least area of PCB. 2.4 GHz Wi-Fi plus Bluetooth dual-mode chip, with TSMC Ultra-low power consumption 40nm technology,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
